// Digital circuit Acc8-seq.dig as structural Verilog
module Acc8_seq (
  input  EN,
  input  RST,
  input  CLK,
  output [7:0] R,
  output OVF
);

  wire and_1_out, and_2_out, comparator_1_gt, comparator_2_lt, counter_1_ovf, d_ff_1_q;
  wire [3:0] counter_1_out;
  wire [7:0] rom_1_d;

  Counter #(.Bits(4)) counter_1 (.en(EN), .C(CLK), .clr(RST), .out(counter_1_out), .ovf(counter_1_ovf));
  and and_1 (and_1_out, EN, ~d_ff_1_q);  // And
  ROM #(.AddrBits(4), .Bits(8)) rom_1 (.A(counter_1_out), .sel(and_1_out), .D(rom_1_d));
  Comparator #(.Bits(8)) comparator_1 (.a(rom_1_d), .b(8'h55), .gt(comparator_1_gt));  // open: eq, lt
  Comparator #(.Bits(8)) comparator_2 (.a(rom_1_d), .b({8{1'b0}}), .lt(comparator_2_lt));  // open: gt, eq
  D_FF d_ff_1 (.D(1'b1), .C(comparator_1_gt), .Q(d_ff_1_q));  // open: nQ
  and and_2 (and_2_out, EN, ~comparator_2_lt);  // And
  Acc8 acc8_1 (.A(rom_1_d), .EN(and_2_out), .RST(RST), .Clk(CLK), .R(R), .OVF(OVF));

  // Notes on the sheet:
  //   contents of rom_1 (hex, n*v repeats v):
  //   1,2,4,25,5,a6,0,2b,c1,9,21,76,f2
endmodule
