// Digital circuit Acc8.dig as structural Verilog
module Acc8 (
  input  [7:0] A,
  input  EN,
  input  RST,
  input  Clk,
  output [7:0] R,
  output OVF
);

  wire and_1_out;
  wire [7:0] addsub8_ovf_1_r;

  AddSub8_ovf addsub8_ovf_1 (.AS(RST), .B(R), .A(A), .R(addsub8_ovf_1_r), .OVF(OVF));
  and and_1 (and_1_out, EN, ~OVF);  // And
  Reg8 reg8_1 (.clk(Clk), .D(addsub8_ovf_1_r), .rst(RST), .en(and_1_out), .Q(R));
endmodule
