// Digital circuit AddSub8-ovf.dig as structural Verilog
module AddSub8_ovf (
  input  AS,
  input  [7:0] B,
  input  [7:0] A,
  output [7:0] R,
  output OVF
);

  wire add8_1_co, xnor_1_out, xor_9_out;
  wire [7:0] xor_1_out;

  xor xor_1 (xor_1_out[0], B[0], AS);
  xor xor_2 (xor_1_out[1], B[1], AS);
  xor xor_3 (xor_1_out[2], B[2], AS);
  xor xor_4 (xor_1_out[3], B[3], AS);
  xor xor_5 (xor_1_out[4], AS, B[4]);
  xor xor_6 (xor_1_out[5], AS, B[5]);
  xor xor_7 (xor_1_out[6], AS, B[6]);
  xor xor_8 (xor_1_out[7], AS, B[7]);
  Add8 add8_1 (.A(A), .B(xor_1_out), .Ci(AS), .Co(add8_1_co), .S(R));
  xnor xnor_1 (xnor_1_out, A[7], xor_1_out[7]);
  xor xor_9 (xor_9_out, R[7], xnor_1_out);
  and and_1 (OVF, add8_1_co, xor_9_out);
endmodule
