// Digital circuit Add8.dig as structural Verilog
module Add8 (
  input  [7:0] A,
  input  [7:0] B,
  input  Ci,
  output Co,
  output [7:0] S
);

  wire fa_2_co, fa_3_co, fa_4_co, fa_5_co, fa_6_co, fa_7_co, fa_8_co;

  FA fa_1 (.A(A[7]), .B(B[7]), .Ci(fa_2_co), .S(S[7]), .Co(Co));
  FA fa_2 (.A(A[6]), .B(B[6]), .Ci(fa_3_co), .S(S[6]), .Co(fa_2_co));
  FA fa_3 (.A(A[5]), .B(B[5]), .Ci(fa_4_co), .S(S[5]), .Co(fa_3_co));
  FA fa_4 (.A(A[4]), .B(B[4]), .Ci(fa_5_co), .S(S[4]), .Co(fa_4_co));
  FA fa_5 (.A(A[3]), .B(B[3]), .Ci(fa_6_co), .S(S[3]), .Co(fa_5_co));
  FA fa_6 (.A(A[2]), .B(B[2]), .Ci(fa_7_co), .S(S[2]), .Co(fa_6_co));
  FA fa_7 (.A(A[1]), .B(B[1]), .Ci(fa_8_co), .S(S[1]), .Co(fa_7_co));
  FA fa_8 (.A(A[0]), .B(B[0]), .Ci(Ci), .S(S[0]), .Co(fa_8_co));
endmodule
