// Digital circuit Reg8.dig as structural Verilog
module Reg8 (
  input  clk,
  input  [7:0] D,
  input  rst,
  input  en,
  output [7:0] Q
);

  wire and_1_out;

  and and_1 (and_1_out, clk, en);
  D_FF_AS #(.Bits(8)) d_ff_as_1 (.Set(1'b0), .D(D), .C(and_1_out), .Clr(rst), .Q(Q));  // open: nQ

  // Notes on the sheet:
  //   Registo de 8 bits com enable e reset assíncrono
endmodule
